# Fritzing sketch ping pong light for print 2up (saved by Fritzing 0.7.12b)
breadboards: 1

parts:
  U1 = attiny85 [package=dip]
  LED1 = RGB LED (com. anode, rbg) [package="5 mm [THT]"]
  J3 = female pin header, 1 pin [form="♀ (female)"]
  J4 = female pin header, 1 pin [form="♀ (female)"]
  S1 = Pushbutton [package="[THT]"]
  R1 = Resistor [tolerance=±5% resistance=220 package=THT]
  U2 = attiny85 [package=dip]
  LED2 = RGB LED (com. anode, rbg) [package="5 mm [THT]"]
  J5 = female pin header, 1 pin [form="♀ (female)"]
  J6 = female pin header, 1 pin [form="♀ (female)"]
  S2 = Pushbutton [package="[THT]"]
  R2 = Resistor [tolerance=±5% resistance=220 package=THT]

nets:
  N1: U1.Pin_3, LED1.red_cathode
  N2: U1.Pin_4, J3.pin1, R1.Pin_1
  N3: U1.Pin_5, LED1.blue_cathode
  N4: U1.Pin_6, LED1.green_cathode
  N5: U1.Pin_7, S1.Pin_3, S1.Pin_4, R1.Pin_0
  N6: U1.Pin_8, LED1.common_anode, J4.pin1, S1.Pin_1, S1.Pin_2
  N7: U2.Pin_3, LED2.red_cathode
  N8: U2.Pin_4, J5.pin1, R2.Pin_1
  N9: U2.Pin_5, LED2.blue_cathode
  N10: U2.Pin_6, LED2.green_cathode
  N11: U2.Pin_7, S2.Pin_3, S2.Pin_4, R2.Pin_0
  N12: U2.Pin_8, LED2.common_anode, J6.pin1, S2.Pin_1, S2.Pin_2
