# Fritzing sketch ping pong light (saved by Fritzing 0.7.12b)
breadboards: 1

parts:
  U1 = attiny85 [package=dip]
  LED1 = RGB LED (com. anode, rbg) [package="5 mm [THT]"]
  S1 = Pushbutton [package="[THT]"]
  R1 = Resistor [tolerance=±5% resistance=220 package=THT]

nets:
  N1: U1.Pin_3, LED1.red_cathode
  N2: U1.Pin_4, R1.Pin_1
  N3: U1.Pin_5, LED1.blue_cathode
  N4: U1.Pin_6, LED1.green_cathode
  N5: U1.Pin_7, S1.Pin_3, S1.Pin_4, R1.Pin_0
  N6: U1.Pin_8, LED1.common_anode, S1.Pin_1, S1.Pin_2
